// Logisim project ProjetoULAFinal.circ as structural Verilog
module Projeto_ULA (
  input  [7:0] A,
  input  [7:0] B,
  input  [2:0] in_3,
  input  [2:0] in_4,
  input  [3:0] Opcode,
  output [7:0] S
);

  wire [7:0] and_1_out, multiplier_1_out, nand_1_out, nor_1_out, not_1_out, or_1_out, shifter_1_out,
       shifter_2_out, somador_8bits_1_s, subtrator_8bits_1_s, xnor_1_out, xor_1_out;

  Multiplier multiplier_1 (.a(A), .b(B), .out(multiplier_1_out));  // open: cin, cout
  assign not_1_out = ~A;  // NOT_Gate not_1, 8 bits wide
  assign nand_1_out = ~(A & B);  // NAND_Gate nand_1, 8 bits wide
  Somador_8Bits somador_8bits_1 (.S(somador_8bits_1_s), .A(A), .B(B));
  assign or_1_out = A | B;  // OR_Gate or_1, 8 bits wide
  assign xnor_1_out = ~(A ^ B);  // XNOR_Gate xnor_1, 8 bits wide
  Shifter shifter_1 (.in(A), .\dist (in_4), .out(shifter_1_out));
  assign xor_1_out = A ^ B;  // XOR_Gate xor_1, 8 bits wide
  assign and_1_out = A & B;  // AND_Gate and_1, 8 bits wide
  assign nor_1_out = ~(A | B);  // NOR_Gate nor_1, 8 bits wide
  Subtrator_8Bits subtrator_8bits_1 (.S(subtrator_8bits_1_s), .A(A), .B(B));
  Shifter #(.shift("lr")) shifter_2 (.in(A), .\dist (in_3), .out(shifter_2_out));
  Multiplexer #(.select(4), .width(8), .enable("false")) multiplexer_1 (
    .in0({8{1'b0}}), .in1(subtrator_8bits_1_s), .in2(multiplier_1_out), .in3({8{1'b0}}), .in4(shifter_2_out),
    .in5(nand_1_out), .in6({8{1'b0}}), .in7(somador_8bits_1_s), .in8(not_1_out), .in9(or_1_out),
    .in10(xnor_1_out), .in11(shifter_1_out), .in12(xor_1_out), .in13({8{1'b0}}), .in14(and_1_out),
    .in15(nor_1_out), .out(S), .sel(Opcode));
endmodule

module Ex1_Relatorio2 (
  input  [3:0] A,
  input  [3:0] B,
  input  Cin,
  output Cout,
  output [3:0] S
);

  wire multiplexer_1_out, multiplexer_2_out, multiplexer_3_out, multiplexer_4_out, not_1_out, not_2_out,
       not_3_out, not_4_out, somador_completo_2_cout, somador_completo_3_cout, somador_completo_4_cout;

  not not_1 (not_1_out, B[3]);
  Multiplexer #(.enable("false")) multiplexer_1 (.in0(B[3]), .in1(not_1_out), .out(multiplexer_1_out), .sel(Cin));
  Somador_Completo somador_completo_1 (
    .Cout(Cout), .S(S[3]), .B(multiplexer_1_out), .A(A[3]), .Cin(somador_completo_2_cout));
  not not_2 (not_2_out, B[2]);
  Multiplexer #(.enable("false")) multiplexer_2 (.in0(B[2]), .in1(not_2_out), .out(multiplexer_2_out), .sel(Cin));
  Somador_Completo somador_completo_2 (
    .Cout(somador_completo_2_cout), .S(S[2]), .B(multiplexer_2_out), .A(A[2]), .Cin(somador_completo_3_cout));
  not not_3 (not_3_out, B[1]);
  Multiplexer #(.enable("false")) multiplexer_3 (.in0(B[1]), .in1(not_3_out), .out(multiplexer_3_out), .sel(Cin));
  Somador_Completo somador_completo_3 (
    .Cout(somador_completo_3_cout), .S(S[1]), .B(multiplexer_3_out), .A(A[1]), .Cin(somador_completo_4_cout));
  not not_4 (not_4_out, B[0]);
  Multiplexer #(.enable("false")) multiplexer_4 (.in0(B[0]), .in1(not_4_out), .out(multiplexer_4_out), .sel(Cin));
  Somador_Completo somador_completo_4 (
    .Cout(somador_completo_4_cout), .S(S[0]), .B(multiplexer_4_out), .A(A[0]), .Cin(Cin));
endmodule

module Ex2_Relatorio2 (
  input  A1,
  input  A0,
  input  B1,
  input  B0,
  output P3,
  output P2,
  output P1,
  output P0
);

  wire and_1_out, and_2_out, and_3_out, meio_somador_2_cout;

  and and_1 (and_1_out, A1, B1);
  and and_2 (and_2_out, A1, B0);
  Meio_Somador meio_somador_1 (.A(meio_somador_2_cout), .Cout(P3), .B(and_1_out), .S(P2));
  and and_3 (and_3_out, A0, B1);
  Meio_Somador meio_somador_2 (.A(and_3_out), .Cout(meio_somador_2_cout), .B(and_2_out), .S(P1));
  and and_4 (P0, A0, B0);
endmodule

module Ex3_Relatorio2 (
  input  [3:0] D,
  input  CLK,
  input  Carga,
  input  Clear,
  output [3:0] Q
);

  wire multiplexer_1_out, multiplexer_2_out, multiplexer_3_out, multiplexer_4_out;

  Multiplexer #(.enable("false")) multiplexer_1 (.in0(Q[3]), .in1(D[3]), .out(multiplexer_1_out), .sel(Carga));
  D_Flip_Flop d_ff_1 (.D(multiplexer_1_out), .clk(CLK), .Q(Q[3]), .reset(Clear));  // open: Qn, preset
  Multiplexer #(.enable("false")) multiplexer_2 (.in0(Q[2]), .in1(D[2]), .out(multiplexer_2_out), .sel(Carga));
  D_Flip_Flop d_ff_2 (.D(multiplexer_2_out), .clk(CLK), .Q(Q[2]), .reset(Clear));  // open: Qn, preset
  Multiplexer #(.enable("false")) multiplexer_3 (.in0(Q[1]), .in1(D[1]), .out(multiplexer_3_out), .sel(Carga));
  D_Flip_Flop d_ff_3 (.D(multiplexer_3_out), .clk(CLK), .Q(Q[1]), .reset(Clear));  // open: Qn, preset
  D_Flip_Flop d_ff_4 (.D(multiplexer_4_out), .clk(CLK), .Q(Q[0]), .reset(Clear));  // open: Qn, preset
  Multiplexer #(.enable("false")) multiplexer_4 (.in0(Q[0]), .in1(D[0]), .out(multiplexer_4_out), .sel(Carga));
endmodule

module main (
  input  [3:0] in_1,
  input  [3:0] in_2,
  input  [3:0] in_3,
  input  [3:0] in_4,
  input  [1:0] in_5,
  output [3:0] out_6
);

  Multiplexer #(.select(2), .width(4), .enable("false")) multiplexer_1 (
    .in0(in_1), .in1(in_2), .in2(in_3), .in3(in_4), .out(out_6), .sel(in_5));
endmodule

module Meio_Somador (
  input  A,
  input  B,
  output S,
  output Cout
);

  and and_1 (Cout, A, B);
  xor xor_1 (S, A, B);
endmodule

module Somador_Completo (
  input  A,
  input  B,
  input  Cin,
  output S,
  output Cout
);

  wire meio_somador_1_cout, meio_somador_1_s, meio_somador_2_cout;

  Meio_Somador meio_somador_1 (.A(A), .Cout(meio_somador_1_cout), .B(B), .S(meio_somador_1_s));
  Meio_Somador meio_somador_2 (.A(meio_somador_1_s), .Cout(meio_somador_2_cout), .B(Cin), .S(S));
  or or_1 (Cout, meio_somador_2_cout, meio_somador_1_cout);
endmodule

module Somador_4Bits (
  input  [3:0] A,
  input  [3:0] B,
  output [3:0] S
);

  wire somador_completo_1_cout, somador_completo_2_cout, somador_completo_3_cout, somador_completo_4_cout;

  Somador_Completo somador_completo_1 (
    .Cout(somador_completo_1_cout), .S(S[3]), .B(B[3]), .A(A[3]), .Cin(somador_completo_2_cout));
  Hex_Digit_Display hex_digit_display_1 (.value(S));  // open: dp
  Somador_Completo somador_completo_2 (
    .Cout(somador_completo_2_cout), .S(S[2]), .B(B[2]), .A(A[2]), .Cin(somador_completo_3_cout));
  Somador_Completo somador_completo_3 (
    .Cout(somador_completo_3_cout), .S(S[1]), .B(B[1]), .A(A[1]), .Cin(somador_completo_4_cout));
  Somador_Completo somador_completo_4 (.Cout(somador_completo_4_cout), .S(S[0]), .B(B[0]), .A(A[0]), .Cin(1'b0));
  // also tied to GND on the sheet: somador_completo_1_cout
endmodule

module Meio_Subtrator (
  input  A,
  input  B,
  output S,
  output Tout
);

  wire not_1_out;

  not not_1 (not_1_out, A);
  xor xor_1 (S, A, B);
  and and_1 (Tout, B, not_1_out);
endmodule

module Subtrator_Completo (
  input  A,
  input  B,
  input  Bin,
  output S,
  output Bout
);

  wire meio_subtrator_1_s, meio_subtrator_1_tout, meio_subtrator_2_tout;

  Meio_Subtrator meio_subtrator_1 (.B(B), .Tout(meio_subtrator_1_tout), .A(A), .S(meio_subtrator_1_s));
  Meio_Subtrator meio_subtrator_2 (.B(Bin), .Tout(meio_subtrator_2_tout), .A(meio_subtrator_1_s), .S(S));
  or or_1 (Bout, meio_subtrator_2_tout, meio_subtrator_1_tout);
endmodule

module Exercicio_1 (
  input  in_1,
  input  in_2,
  input  in_3,
  input  in_4,
  input  in_5,
  input  in_6,
  input  in_7,
  input  in_8,
  input  in_9,
  output out_10,
  output out_11
);

  wire meio_somador_1_s, meio_somador_2_cout, meio_subtrator_1_s, meio_subtrator_2_tout;

  Meio_Somador meio_somador_1 (.A(in_1), .B(in_2), .S(meio_somador_1_s));  // open: Cout
  Meio_Subtrator meio_subtrator_1 (.B(in_4), .A(in_3), .S(meio_subtrator_1_s));  // open: Tout
  Meio_Somador meio_somador_2 (.A(in_5), .Cout(meio_somador_2_cout), .B(in_6));  // open: S
  Meio_Subtrator meio_subtrator_2 (.B(in_8), .Tout(meio_subtrator_2_tout), .A(in_7));  // open: S
  Multiplexer #(.enable("false")) multiplexer_1 (
    .in0(meio_somador_1_s), .in1(meio_subtrator_1_s), .out(out_10), .sel(in_9));
  Multiplexer #(.enable("false")) multiplexer_2 (
    .in0(meio_somador_2_cout), .in1(meio_subtrator_2_tout), .out(out_11), .sel(in_9));
endmodule

module Subtrator_8Bits (
  input  [7:0] A,
  input  [7:0] B,
  output [7:0] S
);

  wire subtrator_completo_1_bout, subtrator_completo_2_bout, subtrator_completo_3_bout,
       subtrator_completo_4_bout, subtrator_completo_5_bout, subtrator_completo_6_bout,
       subtrator_completo_7_bout, subtrator_completo_8_bout;

  Subtrator_Completo subtrator_completo_1 (
    .Bout(subtrator_completo_1_bout), .Bin(subtrator_completo_2_bout), .S(S[7]), .A(A[7]), .B(B[7]));
  Subtrator_Completo subtrator_completo_2 (
    .Bout(subtrator_completo_2_bout), .Bin(subtrator_completo_3_bout), .S(S[6]), .A(A[6]), .B(B[6]));
  Subtrator_Completo subtrator_completo_3 (
    .Bout(subtrator_completo_3_bout), .Bin(subtrator_completo_4_bout), .S(S[5]), .A(A[5]), .B(B[5]));
  Subtrator_Completo subtrator_completo_4 (
    .Bout(subtrator_completo_4_bout), .Bin(subtrator_completo_5_bout), .S(S[4]), .A(A[4]), .B(B[4]));
  Subtrator_Completo subtrator_completo_5 (
    .Bout(subtrator_completo_5_bout), .Bin(subtrator_completo_6_bout), .S(S[3]), .A(A[3]), .B(B[3]));
  Subtrator_Completo subtrator_completo_6 (
    .Bout(subtrator_completo_6_bout), .Bin(subtrator_completo_7_bout), .S(S[2]), .A(A[2]), .B(B[2]));
  Subtrator_Completo subtrator_completo_7 (
    .Bout(subtrator_completo_7_bout), .Bin(subtrator_completo_8_bout), .S(S[1]), .A(A[1]), .B(B[1]));
  Subtrator_Completo subtrator_completo_8 (.Bout(subtrator_completo_8_bout), .Bin(1'b0), .S(S[0]), .A(A[0]), .B(B[0]));
  // also tied to GND on the sheet: subtrator_completo_1_bout
endmodule

module Somador_8Bits (
  input  [7:0] A,
  input  [7:0] B,
  output [7:0] S
);

  wire somador_completo_1_cout, somador_completo_2_cout, somador_completo_3_cout, somador_completo_4_cout,
       somador_completo_5_cout, somador_completo_6_cout, somador_completo_7_cout, somador_completo_8_cout;

  Somador_Completo somador_completo_1 (
    .Cout(somador_completo_1_cout), .S(S[7]), .B(B[7]), .A(A[7]), .Cin(somador_completo_2_cout));
  Somador_Completo somador_completo_2 (
    .Cout(somador_completo_2_cout), .S(S[6]), .B(B[6]), .A(A[6]), .Cin(somador_completo_3_cout));
  Somador_Completo somador_completo_3 (
    .Cout(somador_completo_3_cout), .S(S[5]), .B(B[5]), .A(A[5]), .Cin(somador_completo_4_cout));
  Somador_Completo somador_completo_4 (
    .Cout(somador_completo_4_cout), .S(S[4]), .B(B[4]), .A(A[4]), .Cin(somador_completo_5_cout));
  Somador_Completo somador_completo_5 (
    .Cout(somador_completo_5_cout), .S(S[3]), .B(B[3]), .A(A[3]), .Cin(somador_completo_6_cout));
  Somador_Completo somador_completo_6 (
    .Cout(somador_completo_6_cout), .S(S[2]), .B(B[2]), .A(A[2]), .Cin(somador_completo_7_cout));
  Somador_Completo somador_completo_7 (
    .Cout(somador_completo_7_cout), .S(S[1]), .B(B[1]), .A(A[1]), .Cin(somador_completo_8_cout));
  Somador_Completo somador_completo_8 (.Cout(somador_completo_8_cout), .S(S[0]), .B(B[0]), .A(A[0]), .Cin(1'b0));
  // also tied to GND on the sheet: somador_completo_1_cout
endmodule
