// Logisim project Relatorio_01_Ewel.circ as structural Verilog: 6 circuits, main circuit meioSomador
module meioSomador (
  input  A,
  input  B,
  output S,
  output Cout
);

  xor xor_1 (S, A, B);
  and and_1 (Cout, A, B);
endmodule

module meioSubtrator (
  input  A,
  input  B,
  output S,
  output Tout
);

  wire not_1_out;

  not not_1 (not_1_out, A);
  xor xor_1 (S, A, B);
  and and_1 (Tout, B, not_1_out);
endmodule

module subtratorCompleto (
  input  A,
  input  B,
  input  Bin,
  output S,
  output Bout
);

  wire meiosubtrator_1_s, meiosubtrator_1_tout, meiosubtrator_2_tout;

  meioSubtrator meiosubtrator_1 (.Tout(meiosubtrator_1_tout), .B(B), .S(meiosubtrator_1_s), .A(A));
  meioSubtrator meiosubtrator_2 (.Tout(meiosubtrator_2_tout), .B(Bin), .S(S), .A(meiosubtrator_1_s));
  or or_1 (Bout, meiosubtrator_2_tout, meiosubtrator_1_tout);
endmodule

module somadorCompleto (
  input  A,
  input  B,
  input  Cin,
  output S,
  output Cout
);

  wire meiosomador_1_cout, meiosomador_1_s, meiosomador_2_cout;

  meioSomador meiosomador_1 (.Cout(meiosomador_1_cout), .B(B), .S(meiosomador_1_s), .A(A));
  meioSomador meiosomador_2 (.Cout(meiosomador_2_cout), .B(Cin), .S(S), .A(meiosomador_1_s));
  or or_1 (Cout, meiosomador_2_cout, meiosomador_1_cout);
endmodule

module Ex01 (
  input  [1:0] in_1,
  input  in_2,
  output [1:0] out_3
);

  wire [1:0] demultiplexer_1_out0, demultiplexer_1_out1, meiosomador_1_s, meiosubtrator_1_s;

  Demultiplexer #(.width(2), .enable("false")) demultiplexer_1 (
    .out0(demultiplexer_1_out0), .out1(demultiplexer_1_out1), .in(in_1), .sel(in_2));
  meioSomador meiosomador_1 (
    .Cout(meiosomador_1_s[1]), .B(demultiplexer_1_out0[1]), .S(meiosomador_1_s[0]),
    .A(demultiplexer_1_out0[0]));
  meioSubtrator meiosubtrator_1 (
    .Tout(meiosubtrator_1_s[1]), .B(demultiplexer_1_out1[1]), .S(meiosubtrator_1_s[0]),
    .A(demultiplexer_1_out1[0]));
  Multiplexer #(.width(2), .enable("false")) multiplexer_1 (
    .in0(meiosomador_1_s), .in1(meiosubtrator_1_s), .out(out_3), .sel(in_2));
endmodule

module Ex02 (
  input  [2:0] in_1,
  input  in_2,
  output [1:0] out_3
);

  wire [1:0] somadorcompleto_1_s, subtratorcompleto_1_s;
  wire [2:0] demultiplexer_1_out0, demultiplexer_1_out1;

  Demultiplexer #(.width(3), .enable("false")) demultiplexer_1 (
    .out0(demultiplexer_1_out0), .out1(demultiplexer_1_out1), .in(in_1), .sel(in_2));
  somadorCompleto somadorcompleto_1 (
    .Cout(somadorcompleto_1_s[1]), .S(somadorcompleto_1_s[0]), .Cin(demultiplexer_1_out0[2]),
    .B(demultiplexer_1_out0[1]), .A(demultiplexer_1_out0[0]));
  subtratorCompleto subtratorcompleto_1 (
    .Bout(subtratorcompleto_1_s[1]), .S(subtratorcompleto_1_s[0]), .Bin(demultiplexer_1_out1[2]),
    .B(demultiplexer_1_out1[1]), .A(demultiplexer_1_out1[0]));
  Multiplexer #(.width(2), .enable("false")) multiplexer_1 (
    .in0(somadorcompleto_1_s), .in1(subtratorcompleto_1_s), .out(out_3), .sel(in_2));
endmodule
