// Logisim project Relatorio_02_Ewel.circ as structural Verilog
module meioSomador (
  input  A,
  input  B,
  output S,
  output Cout
);

  xor xor_1 (S, A, B);
  and and_1 (Cout, A, B);
endmodule

module somadorCompleto (
  input  A,
  input  B,
  input  Cin,
  output S,
  output Cout
);

  wire meiosomador_1_s, undriven, undriven_2;

  meioSomador meiosomador_1 (.S(meiosomador_1_s));  // open: Cout, B, A
  meioSomador meiosomador_2 (.S(S));  // open: Cout, B, A
  or or_1 (Cout, undriven_2, undriven);
endmodule

module complementoDois (
  input  [3:0] A,
  input  [3:0] B,
  input  Cin,
  output Cout,
  output [3:0] S
);

  wire multiplexer_1_out, multiplexer_2_out, multiplexer_3_out, multiplexer_4_out, not_1_out, not_2_out,
       not_3_out, not_5_out, somadorcompleto_2_cout, somadorcompleto_3_cout, somadorcompleto_4_cout;

  not not_1 (not_1_out, B[3]);
  Multiplexer #(.enable("false")) multiplexer_1 (.in0(B[3]), .in1(not_1_out), .out(multiplexer_1_out), .sel(Cin));
  somadorCompleto somadorcompleto_1 (
    .Cout(Cout), .S(S[3]), .Cin(somadorcompleto_2_cout), .B(multiplexer_1_out), .A(A[3]));
  not not_2 (not_2_out, B[2]);
  Multiplexer #(.enable("false")) multiplexer_2 (.in0(B[2]), .in1(not_2_out), .out(multiplexer_2_out), .sel(Cin));
  somadorCompleto somadorcompleto_2 (
    .Cout(somadorcompleto_2_cout), .S(S[2]), .Cin(somadorcompleto_3_cout), .B(multiplexer_2_out), .A(A[2]));
  Multiplexer #(.enable("false")) multiplexer_3 (.in0(B[1]), .in1(not_3_out), .out(multiplexer_3_out), .sel(Cin));
  not not_3 (not_3_out, B[1]);
  not not_4 (not_3_out, B[1]);
  somadorCompleto somadorcompleto_3 (
    .Cout(somadorcompleto_3_cout), .S(S[1]), .Cin(somadorcompleto_4_cout), .B(multiplexer_3_out), .A(A[1]));
  not not_5 (not_5_out, B[0]);
  Multiplexer #(.enable("false")) multiplexer_4 (.in0(B[0]), .in1(not_5_out), .out(multiplexer_4_out), .sel(Cin));
  somadorCompleto somadorcompleto_4 (
    .Cout(somadorcompleto_4_cout), .S(S[0]), .Cin(Cin), .B(multiplexer_4_out), .A(A[0]));
endmodule

module multiplicador (
  input  A1,
  input  A0,
  input  B1,
  input  B0,
  output P3,
  output P2,
  output P1,
  output P0
);

  wire and_1_out, and_2_out, and_3_out, meiosomador_2_cout;

  and and_1 (and_1_out, A1, B1);
  meioSomador meiosomador_1 (.Cout(P3), .S(P2), .B(and_1_out), .A(meiosomador_2_cout));
  and and_2 (and_2_out, A1, B0);
  and and_3 (and_3_out, A0, B1);
  meioSomador meiosomador_2 (.Cout(meiosomador_2_cout), .S(P1), .B(and_2_out), .A(and_3_out));
  and and_4 (P0, A0, B0);
endmodule

module registrador (
  input  [3:0] D,
  input  Clock,
  input  Carga,
  input  Clear,
  output [3:0] Q
);

  wire multiplexer_1_out, multiplexer_2_out, multiplexer_3_out, multiplexer_4_out;

  D_Flip_Flop d_ff_1 (.D(multiplexer_1_out), .clk(Clock), .Q(Q[0]), .reset(Clear));  // open: Qn, preset
  Multiplexer #(.enable("false")) multiplexer_1 (.in0(Q[0]), .in1(D[0]), .out(multiplexer_1_out), .sel(Carga));
  Multiplexer #(.enable("false")) multiplexer_2 (.in0(Q[1]), .in1(D[1]), .out(multiplexer_2_out), .sel(Carga));
  D_Flip_Flop d_ff_2 (.D(multiplexer_2_out), .clk(Clock), .Q(Q[1]), .reset(Clear));  // open: Qn, preset
  D_Flip_Flop d_ff_3 (.D(multiplexer_3_out), .clk(Clock), .Q(Q[2]), .reset(Clear));  // open: Qn, preset
  Multiplexer #(.enable("false")) multiplexer_3 (.in0(Q[2]), .in1(D[2]), .out(multiplexer_3_out), .sel(Carga));
  D_Flip_Flop d_ff_4 (.D(multiplexer_4_out), .clk(Clock), .Q(Q[3]), .reset(Clear));  // open: Qn, preset
  Multiplexer #(.enable("false")) multiplexer_4 (.in0(Q[3]), .in1(D[3]), .out(multiplexer_4_out), .sel(Carga));
endmodule
